// Logisim project отчет_lb1_Alovt (1).circ as structural Verilog: 3 circuits, main circuit main
module main (
  input  in_1,
  input  in_2,
  input  in_3,
  input  in_4,
  output out_5,
  output out_6,
  output out_7,
  output out_8,
  output out_9,
  output [2:0] out_10,
  output out_11,
  output out_12,
  output out_13
);

  Decoder #(.select(3)) decoder_1 (
    .out0(out_5), .out1(out_6), .out2(out_7), .out3(out_8), .out4(out_9), .out5(out_11), .out6(out_12),
    .out7(out_13), .sel({in_4, in_3, in_2}), .en(in_1));

  assign out_10 = {in_4, in_3, in_2};
endmodule

module \задание2  (
  input  in_1,
  input  in_2,
  input  in_3,
  output q1,
  output q2,
  output q3,
  output q4
);

  wire not_1_out, not_2_out, not_3_out;

  not not_1 (not_1_out, in_1);
  not not_2 (not_2_out, in_2);
  not not_3 (not_3_out, in_3);
  and and_1 (q1, in_1, not_2_out, not_3_out);
  and and_2 (q2, in_1, not_2_out, in_3);
  and and_3 (q3, in_1, in_2, not_3_out);
  and and_4 (q4, in_1, in_2, in_3);

  // Notes on the sheet:
  //   E
  //   X1
  //   X2
endmodule

module \задание3_1  (
  input  X1,
  input  in_2,
  input  in_3,
  output Y1,
  output Y2,
  output Y3
);

  wire and_1_out, and_2_out, and_3_out, and_4_out, not_1_out, not_2_out, not_3_out;

  not not_1 (not_1_out, X1);
  not not_2 (not_2_out, in_2);
  not not_3 (not_3_out, in_3);
  and and_1 (and_1_out, X1, in_2);
  and and_2 (and_2_out, not_1_out, not_2_out, not_3_out);
  or or_1 (Y2, X1, in_2, not_3_out);
  and and_3 (and_3_out, not_1_out, in_2);
  and and_4 (and_4_out, X1, not_2_out);
  or or_2 (Y1, and_1_out, and_2_out);
  or or_3 (Y3, and_3_out, and_4_out);

  // Notes on the sheet:
  //   X2
  //   X3
endmodule
